// Digital circuit CS303_HW2.dig as structural Verilog
module CS303_HW2 (
  input  d2,
  input  d1,
  input  d0
);

  wire and_1_out, and_2_out, and_3_out, and_4_out, and_5_out, and_6_out, and_7_out, and_9_out, and_10_out,
       and_11_out, and_12_out, not_1_out, not_2_out, not_3_out, not_4_out, not_5_out, not_6_out, not_7_out,
       not_8_out, not_9_out, not_10_out, not_11_out, not_12_out, not_13_out, or_1_out, or_2_out, or_3_out,
       or_4_out, or_5_out, or_6_out, or_7_out, or_8_out, or_9_out, or_10_out, or_11_out, or_12_out,
       or_13_out, or_14_out, or_15_out;

  or or_1 (or_1_out, d2, d1);
  and and_1 (and_1_out, d2, d1);
  or or_2 (or_2_out, d2, d1);
  or or_3 (or_3_out, d2, d0);
  or or_4 (or_4_out, d1, d0);
  not not_1 (not_1_out, or_1_out);
  and and_2 (and_2_out, d1, d0);
  and and_3 (and_3_out, d2, d0);
  not not_2 (not_2_out, d0);
  and and_4 (and_4_out, d2, d1);
  not not_3 (not_3_out, or_2_out);
  not not_4 (not_4_out, d0);
  not not_5 (not_5_out, or_3_out);
  not not_6 (not_6_out, d2);
  not not_7 (not_7_out, or_4_out);
  not not_8 (not_8_out, d1);
  and and_5 (and_5_out, not_3_out, not_4_out);
  and and_6 (and_6_out, d0, not_1_out);
  and and_7 (and_7_out, not_5_out, d1);
  // And and_8 has open pins: In_1=and_2_out, In_2=not_6_out, out=open
  and and_9 (and_9_out, not_7_out, d2);
  and and_10 (and_10_out, and_3_out, not_8_out);
  and and_11 (and_11_out, and_1_out, not_2_out);
  and and_12 (and_12_out, and_4_out, d0);
  or or_5 (or_5_out, and_5_out, and_7_out);
  or or_6 (or_6_out, and_6_out, and_9_out);
  or or_7 (or_7_out, and_5_out, and_9_out);
  or or_8 (or_8_out, and_10_out, and_11_out);
  or or_9 (or_9_out, and_5_out, and_6_out);
  or or_10 (or_10_out, and_6_out, and_9_out);
  or or_11 (or_11_out, and_10_out, and_11_out);
  not not_9 (not_9_out, or_10_out);
  or or_12 (or_12_out, or_6_out, and_12_out);
  or or_13 (or_13_out, or_5_out, and_11_out);
  or or_14 (or_14_out, or_7_out, or_8_out);
  or or_15 (or_15_out, or_9_out, and_12_out);
  not not_10 (not_10_out, or_11_out);
  not not_11 (not_11_out, and_7_out);
  not not_12 (not_12_out, or_12_out);
  not not_13 (not_13_out, or_15_out);
  Seven_Seg seven_seg_1 (
    .a(not_9_out), .b(not_10_out), .c(not_11_out), .d(not_12_out), .e(or_13_out), .f(or_14_out),
    .g(not_13_out), .dp(1'b0));

  // Notes on the sheet:
  //   number "0"
  //   number "1"
  //   number "2"
  //   number "3"
  //   number "4"
  //   number "5"
  //   number "6"
  //   number "7"
endmodule
