// Digital circuit hw3_q1.dig as structural Verilog
module hw3_q1 (
  input  A_LSB,
  input  B,
  input  C_MSB,
  output Y0,
  output Y1,
  output Y2,
  output Y3,
  output Y4,
  output Y5,
  output Y6,
  output Y7
);

  wire not_1_out;

  not not_1 (not_1_out, C_MSB);
  Demultiplexer #(.Selector_Bits(2)) demultiplexer_1 (
    .sel({B, A_LSB}), .in(not_1_out), .out_0(Y0), .out_1(Y1), .out_2(Y2), .out_3(Y3));
  Demultiplexer #(.Selector_Bits(2)) demultiplexer_2 (
    .sel({B, A_LSB}), .in(C_MSB), .out_0(Y4), .out_1(Y5), .out_2(Y6), .out_3(Y7));
endmodule
