// Digital circuit hw3_q2.dig as structural Verilog
module hw3_q2 (
  input  S2,
  input  S1,
  input  S0,
  output [2:0] out
);

  wire [2:0] multiplexer_1_out, multiplexer_2_out, multiplexer_3_out, multiplexer_4_out, multiplexer_5_out,
       multiplexer_6_out;

  Multiplexer #(.Bits(3)) multiplexer_1 (.sel(S0), .in_0(3'b000), .in_1(3'b001), .out(multiplexer_1_out));
  Multiplexer #(.Bits(3)) multiplexer_2 (.sel(S0), .in_0(3'b010), .in_1(3'b011), .out(multiplexer_2_out));
  Multiplexer #(.Bits(3)) multiplexer_3 (.sel(S0), .in_0(3'b100), .in_1(3'b101), .out(multiplexer_3_out));
  Multiplexer #(.Bits(3)) multiplexer_4 (.sel(S0), .in_0(3'b110), .in_1(3'b111), .out(multiplexer_4_out));
  Multiplexer #(.Bits(3)) multiplexer_5 (
    .sel(S1), .in_0(multiplexer_1_out), .in_1(multiplexer_2_out), .out(multiplexer_5_out));
  Multiplexer #(.Bits(3)) multiplexer_6 (
    .sel(S1), .in_0(multiplexer_3_out), .in_1(multiplexer_4_out), .out(multiplexer_6_out));
  Multiplexer #(.Bits(3)) multiplexer_7 (.sel(S2), .in_0(multiplexer_5_out), .in_1(multiplexer_6_out), .out(out));
endmodule
