// Digital circuit hw3_q3.dig as structural Verilog
module hw3_q3 (
  input  X,
  input  Y,
  input  Z,
  input  X_2,
  input  Y_2,
  input  Z_2,
  output F_x_y_z,
  output F_x_y_z_2
);

  wire decoder_1_out_2, decoder_1_out_3, decoder_1_out_6, decoder_2_out_0, decoder_2_out_1, decoder_2_out_4,
       decoder_2_out_5, decoder_2_out_7, or_1_out, or_2_out, or_3_out, or_4_out, or_5_out;

  Decoder #(.Selector_Bits(3)) decoder_1 (
    .sel({Z_2, Y_2, X_2}), .out_2(decoder_1_out_2), .out_3(decoder_1_out_3), .out_6(decoder_1_out_6));  // open: out_0, out_1, out_4, out_5, out_7
  Decoder #(.Selector_Bits(3)) decoder_2 (
    .sel({Z, Y, X}), .out_0(decoder_2_out_0), .out_1(decoder_2_out_1), .out_4(decoder_2_out_4),
    .out_5(decoder_2_out_5), .out_7(decoder_2_out_7));  // open: out_2, out_3, out_6
  or or_1 (or_1_out, decoder_2_out_0, decoder_2_out_1);
  or or_2 (or_2_out, decoder_2_out_4, decoder_2_out_5);
  or or_3 (or_3_out, decoder_1_out_2, decoder_1_out_3);
  or or_4 (or_4_out, or_1_out, or_2_out);
  or or_5 (or_5_out, or_3_out, decoder_1_out_6);
  not not_1 (F_x_y_z_2, or_5_out);
  or or_6 (F_x_y_z, or_4_out, decoder_2_out_7);
endmodule
