// Digital circuit hw3_q4.dig as structural Verilog
module hw3_q4 (
  input  A,
  input  B,
  input  Cin,
  output SUM,
  output Cout
);

  wire not_1_out;

  not not_1 (not_1_out, Cin);
  Multiplexer #(.Selector_Bits(2)) multiplexer_1 (
    .sel({B, A}), .in_0(Cin), .in_1(not_1_out), .in_2(not_1_out), .in_3(Cin), .out(SUM));
  Multiplexer #(.Selector_Bits(2)) multiplexer_2 (
    .sel({B, A}), .in_0(1'b0), .in_1(Cin), .in_2(Cin), .in_3(1'b1), .out(Cout));
endmodule
