// Digital circuit statemachine.dig as structural Verilog
module statemachine (
  input  A,
  input  B,
  input  CLK,
  output OUT
);

  wire and_1_out, d_ff_1_nq, d_ff_1_q, d_ff_2_q, not_1_out, not_2_out, xor_1_out, xor_2_out, xor_3_out;

  xor xor_1 (xor_1_out, A, B, d_ff_1_q);
  xor xor_2 (xor_2_out, A, B);
  and and_1 (and_1_out, d_ff_1_q, xor_2_out);
  D_FF d_ff_1 (.D(xor_1_out), .C(CLK), .Q(d_ff_1_q), .nQ(d_ff_1_nq));
  D_FF d_ff_2 (.D(xor_3_out), .C(CLK), .Q(d_ff_2_q));  // open: nQ
  xor xor_3 (xor_3_out, d_ff_2_q, and_1_out);
  not not_1 (not_1_out, B);
  not not_2 (not_2_out, A);
  and and_2 (OUT, not_1_out, not_2_out, d_ff_1_nq, d_ff_2_q);
endmodule
