// Digital circuit lab1a.dig as structural Verilog
module lab1a (
  input  in_1,
  input  in_2,
  input  in_3,
  input  in_4,
  input  in_5,
  input  in_6,
  input  in_7,
  input  in_8
);

  wire [3:0] unsignedbcd6_1_p1, unsignedbcd6_1_p3, unsignedbcd_1_p1, unsignedbcd_1_p3, unsignedbcd_2_p1,
       unsignedbcd_2_p3;
  wire [4:0] add_1_s;
  wire [5:5] add_1_c_o;

  Seven_Seg_Hex seven_seg_hex_1 (.d(unsignedbcd_1_p1), .dp(1'b0));
  Seven_Seg_Hex seven_seg_hex_2 (.d(unsignedbcd_1_p3), .dp(1'b0));
  // unsignedBCD unsignedbcd_1: pin names not known; wires that end beside it: unsignedbcd_1_p1, {in_5, in_6, in_7, in_8}, unsignedbcd_1_p3
  Seven_Seg_Hex seven_seg_hex_3 (.d(unsignedbcd_2_p1), .dp(1'b0));
  Add #(.Bits(5)) add_1 (
    .a({1'b0, in_1, in_2, in_3, in_4}), .b({in_5, in_6, in_7, in_8, 1'b0}), .c_i(1'b0), .s(add_1_s),
    .c_o(add_1_c_o[5]));
  Seven_Seg_Hex seven_seg_hex_4 (.d(unsignedbcd_2_p3), .dp(1'b0));
  // unsignedBCD unsignedbcd_2: pin names not known; wires that end beside it: unsignedbcd_2_p1, {in_1, in_2, in_3, in_4}, unsignedbcd_2_p3
  Seven_Seg_Hex seven_seg_hex_5 (.d(unsignedbcd6_1_p1), .dp(1'b0));
  Seven_Seg_Hex seven_seg_hex_6 (.d(unsignedbcd6_1_p3), .dp(1'b0));
  // unsignedBCD6 unsignedbcd6_1: pin names not known; wires that end beside it: unsignedbcd6_1_p1, {add_1_c_o[5], add_1_s}, unsignedbcd6_1_p3

  // Notes on the sheet:
  //   2x
  //   +
  //   =
endmodule
