// Digital circuit abs.dig as structural Verilog
module abs (
  input  [3:0] in,
  output sign,
  output [3:0] out
);

  wire [2:0] xor_3_out;

  xor xor_1 (sign, in[3], 1'b0);
  xor xor_2 (xor_3_out[0], sign, in[0]);
  xor xor_3 (xor_3_out[1], sign, in[1]);
  xor xor_4 (xor_3_out[2], sign, in[2]);
  Add #(.Bits(3)) add_1 (.a(3'b000), .b(xor_3_out), .c_i(sign), .s(out[2:0]), .c_o(out[3]));
endmodule
