// Digital circuit lab2.dig as structural Verilog
module lab2 (
  input  _1,
  input  _2,
  input  _3,
  input  _4,
  output A_MSB,
  output B,
  output C,
  output D_LSB
);

  wire and_1_out, and_2_out, and_3_out, not_1_out, not_2_out, not_3_out, or_1_out, or_2_out, or_3_out;

  and and_1 (and_1_out, _4, _3);
  or or_1 (or_1_out, _3, _4);
  and and_2 (and_2_out, _3, _2);
  or or_2 (or_2_out, _2, _3);
  and and_3 (and_3_out, _1, _2);
  or or_3 (or_3_out, _2, _1);
  not not_1 (not_1_out, and_1_out);
  not not_2 (not_2_out, and_2_out);
  not not_3 (not_3_out, and_3_out);
  and and_4 (C, not_2_out, or_2_out);
  and and_5 (D_LSB, not_3_out, or_3_out);
  and and_6 (B, not_1_out, or_1_out);

  assign A_MSB = _4;
endmodule
