// Digital circuit counter4test.dig as structural Verilog
module counter4test (
  input  clk
);

  wire [3:0] cnt4bcd_1_cnt;

  cnt4BCD cnt4bcd_1 (.CLK(clk), .CNT(cnt4bcd_1_cnt));
  Seven_Seg_Hex seven_seg_hex_1 (.d(cnt4bcd_1_cnt), .dp(1'b0));
endmodule
