// Digital circuit inlab.dig as structural Verilog
module inlab (
  input  clk
);

  wire and_1_out, nor_1_out, not_1_out, not_2_out, upcounter_1_p2;
  wire [3:0] upcounter_1_p5;

  not not_1 (not_1_out, upcounter_1_p2);
  // upcounter upcounter_1: pin names not known; wires that end beside it: not_1_out, upcounter_1_p2, 4'b0101, clk, upcounter_1_p5
  not not_2 (not_2_out, upcounter_1_p5[1]);
  Seven_Seg_Hex seven_seg_hex_1 (.d(upcounter_1_p5), .dp(1'b0));
  and and_1 (and_1_out, upcounter_1_p5[0], not_2_out, upcounter_1_p5[2], upcounter_1_p5[3]);
  or or_1 (upcounter_1_p2, nor_1_out, and_1_out);
  nor nor_1 (nor_1_out, upcounter_1_p5[0], upcounter_1_p5[1], upcounter_1_p5[2], upcounter_1_p5[3]);
endmodule
