// Digital circuit InLab.dig as structural Verilog
module InLab (
  input  clk
);

  wire and_1_out, cntdecud_1_eq_9, not_1_out, not_2_out, not_3_out, not_4_out, t_ff_1_q;
  wire [3:0] cntdecud_1_cnt, cntdecud_2_cnt, d_ff_1_q;

  T_FF t_ff_1 (.T(1'b1), .C(clk), .Q(t_ff_1_q));  // open: nQ
  cntDECud cntdecud_1 (
    .UP(1'b1), .DW(1'b0), .CLK(t_ff_1_q), .RST(1'b1), .CNT(cntdecud_1_cnt), .eq_9(cntdecud_1_eq_9));  // open: eq_0
  not not_1 (not_1_out, and_1_out);
  cntDECud cntdecud_2 (
    .UP(cntdecud_1_eq_9), .DW(1'b0), .CLK(t_ff_1_q), .RST(not_1_out), .CNT(cntdecud_2_cnt));  // open: eq_0, eq_9
  Seven_Seg_Hex seven_seg_hex_1 (.d(cntdecud_2_cnt), .dp(1'b0));
  not not_2 (not_2_out, cntdecud_1_cnt[0]);
  Seven_Seg_Hex seven_seg_hex_2 (.d(d_ff_1_q), .dp(1'b0));
  D_FF #(.Bits(4)) d_ff_1 (.D(cntdecud_1_cnt), .C(not_2_out), .Q(d_ff_1_q));  // open: nQ
  not not_3 (not_3_out, cntdecud_2_cnt[0]);
  not not_4 (not_4_out, cntdecud_2_cnt[3]);
  and and_1 (and_1_out, not_3_out, cntdecud_2_cnt[1], cntdecud_2_cnt[2], not_4_out);

  // Notes on the sheet:
  //   clk: Hz: 2
endmodule
