// Digital circuit PreLab.dig as structural Verilog
module PreLab (
  input  clk,
  input  in_2
);

  wire and_1_out, and_2_out, and_3_out, and_4_out, cntdecud_1_eq_0, cntdecud_1_eq_9, d_ff_1_q, d_ff_2_q,
       DOWN_out, not_1_out, not_2_out, not_3_out, UP_out;
  wire [3:0] cntdecud_1_cnt, cntdecud_2_cnt;

  Button UP (.out(UP_out));
  D_FF d_ff_1 (.D(UP_out), .C(clk), .Q(d_ff_1_q));  // open: nQ
  Button DOWN (.out(DOWN_out));
  D_FF d_ff_2 (.D(DOWN_out), .C(clk), .Q(d_ff_2_q));  // open: nQ
  not not_1 (not_1_out, UP_out);
  not not_2 (not_2_out, DOWN_out);
  and and_1 (and_1_out, not_1_out, d_ff_1_q);
  and and_2 (and_2_out, not_2_out, d_ff_2_q);
  cntDECud cntdecud_1 (
    .UP(and_1_out), .DW(and_2_out), .CLK(clk), .RST(not_3_out), .CNT(cntdecud_1_cnt), .eq_0(cntdecud_1_eq_0),
    .eq_9(cntdecud_1_eq_9));
  not not_3 (not_3_out, in_2);
  and and_3 (and_3_out, cntdecud_1_eq_0, and_2_out);
  Seven_Seg_Hex seven_seg_hex_1 (.d(cntdecud_2_cnt), .dp(1'b0));
  and and_4 (and_4_out, and_1_out, cntdecud_1_eq_9);
  Seven_Seg_Hex seven_seg_hex_2 (.d(cntdecud_1_cnt), .dp(1'b0));
  cntDECud cntdecud_2 (
    .UP(and_4_out), .DW(and_3_out), .CLK(clk), .RST(not_3_out), .CNT(cntdecud_2_cnt));  // open: eq_0, eq_9

  // Notes on the sheet:
  //   clk: Hz: 100
endmodule
