// Digital circuit cntDECud.dig as structural Verilog
module cntDECud (
  input  UP,
  input  DW,
  input  CLK,
  input  RST,
  output [3:0] CNT,
  output eq_0,
  output eq_9
);

  wire and_1_out, and_2_out, and_3_out, and_4_out, and_5_out, and_6_out, and_7_out, and_8_out, and_9_out,
       and_10_out, and_11_out, and_12_out, and_13_out, and_14_out, d_ff_as_1_nq, d_ff_as_2_nq, d_ff_as_3_nq,
       d_ff_as_4_nq, multiplexer_1_out, multiplexer_2_out, multiplexer_3_out, multiplexer_4_out;
  wire [0:0] or_2_out, or_3_out, or_5_out;
  wire [1:0] or_4_out;

  and and_1 (and_1_out, UP, ~DW);  // And
  and and_2 (and_2_out, ~UP, DW);  // And
  and and_3 (and_3_out, and_2_out, eq_0);
  and and_4 (and_4_out, and_1_out, eq_9);
  and and_5 (and_5_out, and_1_out, CNT[0]);
  and and_6 (and_6_out, and_2_out, d_ff_as_1_nq);
  and and_7 (and_7_out, and_5_out, CNT[1]);
  and and_8 (and_8_out, and_6_out, d_ff_as_2_nq);
  and and_9 (and_9_out, and_7_out, CNT[2]);
  and and_10 (and_10_out, and_8_out, d_ff_as_3_nq);
  or or_1 (or_4_out[1], and_3_out, and_4_out);
  and and_11 (and_11_out, and_3_out, ~and_4_out);  // And
  or or_2 (or_2_out[0], and_1_out, and_2_out);
  and and_12 (and_12_out, ~and_3_out, ~and_4_out);  // And
  or or_3 (or_3_out[0], and_5_out, and_6_out);
  and and_13 (and_13_out, ~and_3_out, ~and_4_out);  // And
  or or_4 (or_4_out[0], and_7_out, and_8_out);
  and and_14 (and_14_out, and_3_out, ~and_4_out);  // And
  or or_5 (or_5_out[0], and_9_out, and_10_out);
  Multiplexer #(.Selector_Bits(2)) multiplexer_1 (
    .sel({or_4_out[1], or_2_out[0]}), .in_0(CNT[0]), .in_1(d_ff_as_1_nq), .in_2(and_11_out),
    .in_3(and_11_out), .out(multiplexer_1_out));
  Multiplexer #(.Selector_Bits(2)) multiplexer_2 (
    .sel({or_4_out[1], or_3_out[0]}), .in_0(CNT[1]), .in_1(d_ff_as_2_nq), .in_2(and_12_out),
    .in_3(and_12_out), .out(multiplexer_2_out));
  Multiplexer #(.Selector_Bits(2)) multiplexer_3 (
    .sel(or_4_out), .in_0(CNT[2]), .in_1(d_ff_as_3_nq), .in_2(and_13_out), .in_3(and_13_out),
    .out(multiplexer_3_out));
  Multiplexer #(.Selector_Bits(2)) multiplexer_4 (
    .sel({or_4_out[1], or_5_out[0]}), .in_0(CNT[3]), .in_1(d_ff_as_4_nq), .in_2(and_14_out),
    .in_3(and_14_out), .out(multiplexer_4_out));
  D_FF_AS d_ff_as_1 (.Set(1'b0), .D(multiplexer_1_out), .C(CLK), .Clr(~RST), .Q(CNT[0]), .nQ(d_ff_as_1_nq));
  D_FF_AS d_ff_as_2 (.Set(1'b0), .D(multiplexer_2_out), .C(CLK), .Clr(~RST), .Q(CNT[1]), .nQ(d_ff_as_2_nq));
  D_FF_AS d_ff_as_3 (.Set(1'b0), .D(multiplexer_3_out), .C(CLK), .Clr(~RST), .Q(CNT[2]), .nQ(d_ff_as_3_nq));
  D_FF_AS d_ff_as_4 (.Set(1'b0), .D(multiplexer_4_out), .C(CLK), .Clr(~RST), .Q(CNT[3]), .nQ(d_ff_as_4_nq));
  and and_15 (eq_0, ~CNT[0], ~CNT[1], ~CNT[2], ~CNT[3]);  // And
  and and_16 (eq_9, CNT[0], ~CNT[1], ~CNT[2], CNT[3]);  // And
endmodule
