// Digital circuit project.dig as structural Verilog
module project (
  input  in_1,
  input  clk,
  output [6:0] out_3,
  output [15:0] out_4
);

  wire _0_out, _1_out, _2_out, _3_out, _4_out, _5_out, _6_out, _7_out, _8_out, _9_out, and_1_out, and_2_out,
       ID_2_out, PASS_2_out, u_encoder_da, u_ModeSelector_ido, u_ModeSelector_pwdo, u_shifter_pwd_led1,
       u_shifter_pwd_led2, u_shifter_pwd_led3, u_shifter_pwd_led4, u_shifter_pwd_match, u_timer_dis,
       u_timer_reset;
  wire [3:0] u_encoder_data, u_shifter_id0, u_shifter_id1;

  Button _1 (.out(_1_out));
  Button _4 (.out(_4_out));
  Button _7 (.out(_7_out));
  Button _2 (.out(_2_out));
  Button _5 (.out(_5_out));
  Button _8 (.out(_8_out));
  Button _0 (.out(_0_out));
  Button _3 (.out(_3_out));
  Button _6 (.out(_6_out));
  Button _9 (.out(_9_out));
  LED ID (.in(u_ModeSelector_ido));
  LED PASS (.in(u_ModeSelector_pwdo));
  Button ID_2 (.out(ID_2_out));
  Button PASS_2 (.out(PASS_2_out));
  ModeSelector #(.applicationType("IVERILOG")) u_ModeSelector (
    .ID(ID_2_out), .PWD(PASS_2_out), .DIS(u_timer_dis), .RESET(u_timer_reset), .CLK(clk), .RST(in_1),
    .IDO(u_ModeSelector_ido), .PWDO(u_ModeSelector_pwdo));
  encoder #(.applicationType("IVERILOG")) u_encoder (
    .P0(_0_out), .P1(_1_out), .P2(_2_out), .P3(_3_out), .P4(_4_out), .P5(_5_out), .P6(_6_out), .P7(_7_out),
    .P8(_8_out), .P9(_9_out), .CLK(clk), .RST(in_1), .DATA(u_encoder_data), .DA(u_encoder_da));
  ROM #(.AddrBits(7), .Bits(16)) Password (.A(out_3), .sel(1'b1), .D(out_4));
  timer #(.applicationType("IVERILOG")) u_timer (
    .START(u_shifter_pwd_led4), .CLK(clk), .RST(in_1), .RESET(u_timer_reset), .DIS(u_timer_dis));
  shifter #(.applicationType("IVERILOG")) u_shifter (
    .IN(u_encoder_data), .EN(u_ModeSelector_ido), .DA(u_encoder_da), .CLK(clk), .RST(in_1),
    .ID1(u_shifter_id1), .ID0(u_shifter_id0), .HEX(out_3));
  shifter_pwd #(.applicationType("IVERILOG")) u_shifter_pwd (
    .DATAin(u_encoder_data), .PWDin(out_4), .EN(u_ModeSelector_pwdo), .DA(u_encoder_da), .CLK(clk),
    .RST(in_1), .MATCH(u_shifter_pwd_match), .LED1(u_shifter_pwd_led1), .LED2(u_shifter_pwd_led2),
    .LED3(u_shifter_pwd_led3), .LED4(u_shifter_pwd_led4));
  Seven_Seg_Hex seven_seg_hex_1 (.d(u_shifter_id1), .dp(1'b0));
  Seven_Seg_Hex seven_seg_hex_2 (.d(u_shifter_id0), .dp(1'b0));
  LED led_1 (.in(u_shifter_pwd_led1));
  LED led_2 (.in(u_shifter_pwd_led2));
  and and_1 (and_1_out, u_shifter_pwd_match, u_shifter_pwd_led4);
  and and_2 (and_2_out, ~u_shifter_pwd_match, u_shifter_pwd_led4);  // And
  LED led_3 (.in(u_shifter_pwd_led3));
  LED led_4 (.in(u_shifter_pwd_led4));
  LED GRANTED (.in(and_1_out));
  LED DENIED (.in(and_2_out));

  // Notes on the sheet:
  //   clk: Hz: 100
  //   00028038 Bartu Sisman
  //   00026490 Guney Ali Unal
  //   contents of Password (hex, n*v repeats v):
  //   1234,5678,33*ffff,1919,63*ffff
endmodule

/* Code of ModeSelector:
module ModeSelector(
  input wire ID,          // ID button
  input wire PWD,         // PWD button
  input wire DIS,         // Display Freeze button
  input wire RESET,       // Reset button
  input wire CLK,         // Clock input
  input wire RST,         // Reset signal
  output reg IDO,         // ID output
  output reg PWDO         // PWD output
);
  // Initial state
  initial begin
    IDO = 1;
    PWDO = 0;
  end

  always @(posedge CLK or negedge RST) begin
    if (!RST || RESET) begin
      // Reset the system
      IDO <= 1;
      PWDO <= 0;
    end else if (DIS == 0) begin  // Only proceed if DIS is not high
      // Handle the button presses
      if (ID && !PWD) begin
        IDO <= 1;  
        PWDO <= 0;
      end 
      if (PWD && !ID) begin
        IDO <= 0;
        PWDO <= 1;
      end 
    end
  end
endmodule
*/

/* Code of encoder:
module encoder(
	input P0, P1, P2, P3, P4, P5, P6, P7, P8, P9,
	input CLK, RST,
	output reg [3:0] DATA,
	output reg DA);
	
	reg pressed;
	wire button;

	assign button = P0|P1|P2|P3|P4|P5|P6|P7|P8|P9;

	always @(posedge CLK, negedge RST) 
		if(~RST)
		begin
			pressed <= 0;
			DATA <= 4'b0000;
		end
		else
		begin
			if(button)
			begin
				if(~pressed)
				begin
					pressed <= 1'b1;
					DA <= 1'b1;
				end
				else
					DA <= 1'b0;
				if      (P0) DATA <= 4'b0000;
				else if (P1) DATA <= 4'b0001;
				else if (P2) DATA <= 4'b0010;
				else if (P3) DATA <= 4'b0011;
				else if (P4) DATA <= 4'b0100;
				else if (P5) DATA <= 4'b0101;
				else if (P6) DATA <= 4'b0110;
				else if (P7) DATA <= 4'b0111;
				else if (P8) DATA <= 4'b1000;
				else         DATA <= 4'b1001;
			end
			else
			begin
				pressed <= 1'b0;
				DA <= 1'b0;
			end				
		end			
endmodule
*/

/* Code of timer:
module timer(
    input START,
    input CLK,
    input RST,
    output reg RESET,
    output reg DIS
);
    // 9-bit counter to accommodate 300 (up to 511 can be represented with 9 bits)
    reg [8:0] count = 0;
    parameter COUNT_3_SEC = 300; // For a 100Hz clock, 3 seconds is 300 clock cycles
    reg reset_pulse = 0;

    always @(posedge CLK or negedge RST) begin
        if (!RST) begin
            // Reset everything
            DIS <= 0;
            RESET <= 0;
            count <= 0;
            reset_pulse <= 0;
        end else if (START) begin
            DIS <= 1;
            // Wait for 3 seconds
            if (count < COUNT_3_SEC) begin
                count <= count + 1;
            end else if (count == COUNT_3_SEC && !reset_pulse) begin
                // After 3 seconds, pulse RESET high for one clock cycle
                RESET <= 1;
                reset_pulse <= 1;
            end else begin
                // Then, turn RESET off again and turn DIS off
                RESET <= 0;
                DIS <= 0;
            end
        end else begin
            // If START is not asserted, reset everything
            DIS <= 0;
            RESET <= 0;
            count <= 0;
            reset_pulse <= 0;
        end
    end
endmodule
*/

/* Code of shifter:
module shifter(
    input wire [3:0] IN,
    input wire EN,
    input wire DA,
    input wire CLK,
    input wire RST,
    output reg [3:0] ID1,
    output reg [3:0] ID0,
    output reg [6:0] HEX
);
    // Internal registers for ones and tens digits
    reg [3:0] ones = 4'b0000;
    reg [3:0] tens = 4'b0000;

    always @(posedge CLK or negedge RST) begin
        if (!RST) begin
            // Reset the system
            ones = 4'b0000;
            tens = 4'b0000;
            ID0 = 4'b0000;
            ID1 = 4'b0000;
            HEX = 7'b0000000;
        end else if (EN && DA) begin
            // Shift operation if EN and DA are high
            tens = ones;  // Move ones digit to tens place
            ones = IN;    // Update ones digit
            
            // Output assignments
            ID0 = ones;
            ID1 = tens;
        end else if (EN && !DA) begin
            // If enable is high but data is not available
            // keep the current value in ones and tens
            ID0 = ones;
            ID1 = tens;
        end
    end

    // BCD to binary conversion
    always @(ID0 or ID1) begin
        HEX = ID1 * 10 + ID0;
    end
endmodule
*/

/* Code of shifter_pwd:
module shifter_pwd(
    input wire [3:0] DATAin,
    input wire [15:0] PWDin,
    input wire EN,
    input wire DA,
    input wire CLK,
    input wire RST,
    output reg MATCH,
    output reg LED1,
    output reg LED2,
    output reg LED3,
    output reg LED4
);
    // Internal registers for storing input digits
    reg [15:0] inputDigits = 16'b0000000000000000;

    // Shift operation on positive edge of clock or reset
    always @(posedge CLK or negedge RST) begin
        if (!RST) begin
            // Reset the system
            inputDigits = 16'b0000000000000000;
            MATCH = 0;
            LED1 = 0;
            LED2 = 0;
            LED3 = 0;
            LED4 = 0;
        end else if (EN) begin
            // Shift operation if DA is high
            if (DA) begin
                // Shift previous digits and update ones place with new input
                inputDigits = {inputDigits[11:0], DATAin};

                // Update LED status based on input progress
                LED1 = inputDigits[3:0] != 4'b0000;
                LED2 = inputDigits[7:4] != 4'b0000;
                LED3 = inputDigits[11:8] != 4'b0000;
                LED4 = inputDigits[15:12] != 4'b0000;
            end

            // Check for password match
            MATCH = (inputDigits == PWDin);
        end else if (!EN) begin
            // Reset the system when EN is low
            inputDigits = 16'b0000000000000000;
            MATCH = 0;
            LED1 = 0;
            LED2 = 0;
            LED3 = 0;
            LED4 = 0;
        end
    end
endmodule
*/
